// Digital circuit ALU.dig as structural Verilog
module ALU (
  input  [7:0] A,
  input  [7:0] B,
  input  [2:0] Select,
  output [7:0] Rest,
  output [7:0] Out,
  output Sig
);

  wire [7:0] m0, m1, m02, m2, m3, m4, m5;

  Subtract_negative subtract_negative_1 (.A(A), .B(B), .Subtract(m0), .Sig(Sig));
  // Add_8bits add_8bits_1: pin names not known; wires that end beside it: A, B, m1
  Divider_8bits divider_8bits_1 (.D(A), .d_2(B), .q(m2), .r(m02));
  Times_8bits times_8bits_1 (.A(A[3:0]), .B(B[3:0]), .Times(m3));
  Decrement decrement_1 (.A(A), .Subtract(m4));
  Increment increment_1 (.A(A), .S(m5));  // open: C0
  Multiplexer #(.Selector_Bits(3), .Bits(8)) multiplexer_1 (
    .sel(Select), .in_0({8{1'b0}}), .in_1({8{1'b0}}), .in_2(m02), .in_3({8{1'b0}}), .in_4({8{1'b0}}),
    .in_5({8{1'b0}}), .in_6({8{1'b0}}), .in_7({8{1'b0}}), .out(Rest));
  Multiplexer #(.Selector_Bits(3), .Bits(8)) multiplexer_2 (
    .sel(Select), .in_0(m0), .in_1(m1), .in_2(m2), .in_3(m3), .in_4(m4), .in_5(m5), .in_6({8{1'b0}}),
    .in_7({8{1'b0}}), .out(Out));

  // Other names for the same wires on the sheet: AT[3:0] = A[3:0]; BT[3:0] = B[3:0]; S[2:0] = Select
endmodule
