// Digital circuit ControlUnit.dig as structural Verilog
module ControlUnit (
  input  [3:0] OpCode,
  input  ZF,
  output Pc_load,
  output Pc_inc,
  output [2:0] ALU_sel,
  output AC_Load
);

  wire and_1_out, decoder_1_out_1, decoder_1_out_2, out3, out4, out5, out6, out7, out8, out9;

  Decoder #(.Selector_Bits(4)) decoder_1 (
    .sel(OpCode), .out_1(decoder_1_out_1), .out_2(decoder_1_out_2), .out_3(out3), .out_4(out4), .out_5(out5),
    .out_6(out6), .out_7(out7), .out_8(out8), .out_9(out9));  // open: out_0, out_10, out_11, out_12, out_13, out_14, out_15
  and and_1 (and_1_out, ZF, decoder_1_out_2);
  or or_1 (AC_Load, out8, out7, out9, out6, out5, out4, out3);
  or or_2 (Pc_load, decoder_1_out_1, and_1_out);
  not not_1 (Pc_inc, Pc_load);
  Multiplexer #(.Selector_Bits(4), .Bits(3)) multiplexer_1 (
    .sel(OpCode), .in_0(3'b000), .in_1(3'b000), .in_2(3'b000), .in_3(3'b001), .in_4(3'b000), .in_5(3'b101),
    .in_6(3'b100), .in_7(3'b011), .in_8(3'b010), .in_9(3'b110), .in_10(3'b000), .in_11(3'b000),
    .in_12(3'b000), .in_13(3'b000), .in_14(3'b000), .in_15(3'b000), .out(ALU_sel));
endmodule
