// Digital circuit Decrement.dig as structural Verilog
module Decrement (
  input  [7:0] A,
  output [7:0] Subtract
);

  wire [7:0] add_8bits_1_p3, not_1_out, subtract_8bits_1_p3;

  // Subtract_8bits subtract_8bits_1: pin names not known; wires that end beside it: A, 8'h1, subtract_8bits_1_p3
  assign not_1_out = ~subtract_8bits_1_p3;  // Not not_1, 8 bits wide
  // Add_8bits add_8bits_1: pin names not known; wires that end beside it: not_1_out, 8'h1, add_8bits_1_p3
  assign Subtract = subtract_8bits_1_p3[7] ? add_8bits_1_p3 : 8'bz;  // Driver driver_1
  assign Subtract = ~subtract_8bits_1_p3[7] ? subtract_8bits_1_p3 : 8'bz;  // DriverInvSel driverinvsel_1
  LED led_1 (.in(subtract_8bits_1_p3[7]));
endmodule
