// Digital circuit Increment.dig as structural Verilog
module Increment (
  input  [7:0] A,
  output C0,
  output [7:0] S
);

  wire full_add_1_p5, full_add_2_p5, full_add_3_p5, full_add_4_p5, full_add_5_p5, full_add_6_p5,
       full_add_7_p5;

  // Full_add full_add_1: pin names not known; wires that end beside it: A[0], 1'b1, 1'b0, S[0], full_add_1_p5
  // Full_add full_add_2: pin names not known; wires that end beside it: A[1], 1'b0, full_add_1_p5, S[1], full_add_2_p5
  // Full_add full_add_3: pin names not known; wires that end beside it: A[2], 1'b0, full_add_2_p5, S[2], full_add_3_p5
  // Full_add full_add_4: pin names not known; wires that end beside it: A[3], 1'b0, full_add_3_p5, S[3], full_add_4_p5
  // Full_add full_add_5: pin names not known; wires that end beside it: A[4], 1'b0, full_add_4_p5, S[4], full_add_5_p5
  // Full_add full_add_6: pin names not known; wires that end beside it: A[5], 1'b0, full_add_5_p5, S[5], full_add_6_p5
  // Full_add full_add_7: pin names not known; wires that end beside it: A[6], 1'b0, full_add_6_p5, S[6], full_add_7_p5
  // Full_add full_add_8: pin names not known; wires that end beside it: A[7], 1'b0, full_add_7_p5, S[7], C0

  // Other names for the same wires on the sheet: A1 = A[0]; A2 = A[1]; A3 = A[2]; A4 = A[3]; A5 = A[4]; A6 = A[5];
  //   A7 = A[6]; A8 = A[7]
endmodule
