// Digital circuit Subtract_negative.dig as structural Verilog
module Subtract_negative (
  input  [7:0] A,
  input  [7:0] B,
  output [7:0] Subtract,
  output Sig
);

  wire [6:0] subtract_8bits_1_p3;
  wire [7:0] add_8bits_1_p3, not_1_out;

  // Subtract_8bits subtract_8bits_1: pin names not known; wires that end beside it: A, B, {Sig, subtract_8bits_1_p3}
  assign not_1_out = ~{Sig, subtract_8bits_1_p3};  // Not not_1, 8 bits wide
  // Add_8bits add_8bits_1: pin names not known; wires that end beside it: not_1_out, 8'h1, add_8bits_1_p3
  assign Subtract = Sig ? add_8bits_1_p3 : 8'bz;  // Driver driver_1
  assign Subtract = ~Sig ? {Sig, subtract_8bits_1_p3} : 8'bz;  // DriverInvSel driverinvsel_1
endmodule
