// Digital circuit ZeroFlag.dig as structural Verilog
module ZeroFlag (
  input  [7:0] ac_out,
  output ZF
);

  Comparator #(.Bits(8)) comparator_1 (.a(ac_out), .b({8{1'b0}}), .eq(ZF));  // open: gt, lt
  // Pins of 1 and 8 bits meet at ac_out
endmodule
