// Digital circuit main.dig as structural Verilog
module main (
  input  clk,
  input  IR_teste
);

  wire Pc_inc, Pc_load;
  wire [7:0] In_Ir, IR_q, Pc_out, rom_1_d;

  CounterPreset #(.Bits(8)) Pc (
    .en(Pc_inc), .C(clk), .dir(1'b0), .in(In_Ir), .ld(Pc_load), .clr(1'b0), .out(Pc_out));  // open: ovf
  ROM #(.AddrBits(4), .Bits(8)) rom_1 (.A(Pc_out[3:0]), .sel(1'b1), .D(rom_1_d));
  Register #(.Bits(8)) IR (.D(rom_1_d), .C(clk), .en(IR_teste), .Q(IR_q));
  BitExtender #(.inputBits(4), .outputBits(8)) bitextender_1 (.in(IR_q[7:4]), .out(In_Ir));
  ControlUnit controlunit_1 (.OpCode(IR_q[3:0]), .Pc_load(Pc_load), .Pc_inc(Pc_inc));  // open: ZF, ALU_sel, AC_Load
  // Pins of 4 and 8 bits meet at Pc_out

  // Other names for the same wires on the sheet: Clock = clk

  // Notes on the sheet:
  //   contents of rom_1 (hex, n*v repeats v):
  //   0,3000,e
endmodule
