// Digital circuit main_teste.dig as structural Verilog
module main_teste (
  input  clk,
  input  IR_teste,
  input  Teste_EN,
  input  Teste_LD
);

  wire Pc_inc, Pc_load;
  wire [7:0] In_Ir, IR_q, Pc_out, rom_1_d;

  CounterPreset #(.Bits(8)) Pc (
    .en(Teste_EN), .C(clk), .dir(1'b0), .in({8{1'b0}}), .ld(Teste_LD), .clr(1'b0), .out(Pc_out));  // open: ovf
  ROM #(.AddrBits(8), .Bits(8)) rom_1 (.A(Pc_out), .sel(1'b1), .D(rom_1_d));
  Register #(.Bits(8)) IR (.D(rom_1_d), .C(clk), .en(IR_teste), .Q(IR_q));
  BitExtender #(.inputBits(4), .outputBits(8)) bitextender_1 (.in(IR_q[7:4]), .out(In_Ir));
  ControlUnit controlunit_1 (
    .OpCode(IR_q[3:0]), .ZF(1'b0), .Pc_load(Pc_load), .Pc_inc(Pc_inc));  // open: ALU_sel, AC_Load

  // Other names for the same wires on the sheet: Clock = clk

  // Notes on the sheet:
  //   contents of rom_1 (hex, n*v repeats v):
  //   0,3000,14
endmodule
