// Digital circuit main_v1.dig as structural Verilog
module main_v1 (
  input  clk
);

  wire AC_load, Pc_inc, Pc_load, Signal, zeroflag_1_p1;
  wire [2:0] ALU_sel;
  wire [3:0] IR_q, IR_q_2;
  wire [7:0] In_Ir, Out, Pc_out, Q_ac, Result_rest, rom_1_d;

  CounterPreset #(.Bits(8)) Pc (
    .en(Pc_inc), .C(clk), .dir(1'b0), .in(In_Ir), .ld(Pc_load), .clr(1'b0), .out(Pc_out));  // open: ovf
  ROM #(.AddrBits(8), .Bits(8)) rom_1 (.A(Pc_out), .sel(1'b1), .D(rom_1_d));
  Register #(.Bits(8)) IR (.D(rom_1_d), .C(clk), .en(1'b1), .Q({IR_q_2, IR_q}));
  alucirc alucirc_1 (.A(Q_ac), .B(In_Ir), .Select(ALU_sel), .Rest(Result_rest), .Out(Out), .Sig(Signal));
  BitExtender #(.inputBits(4), .outputBits(8)) bitextender_1 (.in(IR_q), .out(In_Ir));
  // ZeroFlag zeroflag_1: pin names not known; wires that end beside it: zeroflag_1_p1, Q_ac
  ControlUnit controlunit_1 (
    .OpCode(IR_q_2), .ZF(zeroflag_1_p1), .Pc_load(Pc_load), .Pc_inc(Pc_inc), .ALU_sel(ALU_sel),
    .AC_Load(AC_load));
  Register #(.Bits(8)) AC (.D(Out), .C(clk), .en(AC_load), .Q(Q_ac));
  LED led_1 (.in(Signal));
  Seven_Seg_Hex seven_seg_hex_1 (.d(Out[7:4]), .dp(1'b0));
  Seven_Seg_Hex seven_seg_hex_2 (.d(Out[3:0]), .dp(1'b0));
  Seven_Seg_Hex seven_seg_hex_3 (.d(Result_rest[7:4]), .dp(1'b0));
  Seven_Seg_Hex seven_seg_hex_4 (.d(Result_rest[3:0]), .dp(1'b0));

  // Other names for the same wires on the sheet: Clock = clk

  // Notes on the sheet:
  //   contents of rom_1 (hex, n*v repeats v):
  //   92,32,93,44,92,73,97,82,10
endmodule
